# Fritzing sketch locoaddr_detector_v3.1 (saved by Fritzing 1.0.1rc)
circuit board: 10cm x 6.8cm
breadboards: 1

parts:
  J19 = screw terminal, 3 pins
  J21 = Screw terminal - 2 pins [package=THT]
  R14 = Resistor [tolerance=±5% power=0.25W resistance=470 package=THT]
  R13 = Resistor [tolerance=±5% power=0.25W resistance=10k package=THT]
  R12 = Resistor [tolerance=±5% power=0.25W resistance=10k package=THT]
  U5 = SN74LS32N [package="DIP14 [THT]"]
  R15 = Resistor [tolerance=±5% power=0.25W resistance=1k package=THT]
  LED1 = LED - 3mm [color="Green (570nm)" current=0.030A package="3 mm [THT]"]
  C4 = Electrolytic Capacitor [capacitance=100µF voltage=35V package="100 mil [THT, electrolytic]"]
  R17 = Resistor [tolerance=±5% power=0.25W resistance=2.2k package=THT]
  U8 = IC, DIP package, 8 pins [chip_label=6N137]
  R16 = Resistor [tolerance=±5% power=0.25W resistance=270 package=THT]
  R9 = Resistor [tolerance=±5% power=0.25W resistance=1k package=THT]
  R11 = Resistor [tolerance=±5% power=0.25W resistance=470 package=THT]
  R8 = Resistor [tolerance=±5% power=0.25W resistance=100k package=THT]
  C2 = Electrolytic Capacitor [capacitance=100µF voltage=35V package="100 mil [THT, electrolytic]"]
  IC2 = Voltage Regulator 78L05 (TO-92, triangle) [package=to-92]
  IC1 = SN74LS32N [package="DIP14 [THT]"]
  R3 = Resistor [tolerance=±5% power=0.25W resistance=270k package=THT]
  R10 = Resistor [tolerance=±5% power=0.25W resistance=10k package=THT]
  R2 = Resistor [tolerance=±5% power=0.25W resistance=1k package=THT]
  R1 = Resistor [tolerance=±5% power=0.25W resistance=1k package=THT]
  R4 = Resistor [tolerance=±5% power=0.25W resistance=1k package=THT]
  D5 = Diode [part_number=SB320 mn=10 package=diode-1n4001]
  D4 = Diode [part_number=SB320 mn=5 package=diode-1n4001]
  R5 = Resistor [tolerance=±5% power=0.25W resistance=33k package=THT]
  R6 = Resistor [tolerance=±5% power=0.25W resistance=820 package=THT]
  R7 = Resistor [tolerance=±5% power=1W resistance=1.8 package=THT]
  D1 = Rectifier Diode [part_number=1N4007 package="300 mil [THT]"]
  D2 = Rectifier Diode [part_number=1N4007 package="300 mil [THT]"]
  D3 = Rectifier Diode [part_number=1N4007 package="300 mil [THT]"]
  C8 = Film/Foil Capacitor [capacitance=100nF voltage=35V package="5mm [THT, pp]"]
  C7 = Film/Foil Capacitor [capacitance=1nF voltage=35V package="5mm [THT, pp]"]
  C3 = Film/Foil Capacitor [capacitance=100nF voltage=35V package="5mm [THT, pp]"]
  C9 = Film/Foil Capacitor [capacitance=100nF voltage=35V package="5mm [THT, pp]"]
  C6 = Film/Foil Capacitor [capacitance=680pF voltage=35V package="5mm [THT, pp]"]
  C1 = Capacitor Polarized [voltage=35V capacitance=220µF package=cpol-radial-100uf-25v]
  J20 = screw terminal, 2 pins
  R18 = Resistor [tolerance=±5% power=0.25W resistance=1k package=THT]
  R19 = Resistor [tolerance=±5% power=0.25W resistance=1k package=THT]
  C10 = Film/Foil Capacitor [capacitance=100nF voltage=35V package="5mm [THT, pp]"]
  J22 = Screw terminal - 2 pins [package=THT]
  U7 = IC, DIP package, 4 pins [chip_label=PC817]
  C11 = Film/Foil Capacitor [capacitance=100nF voltage=35V package="5mm [THT, pp]"]
  R20 = Resistor [tolerance=±5% power=0.25W resistance=1k package=THT]
  R21 = Resistor [tolerance=±5% power=0.25W resistance=4.7k package=THT]
  R22 = Resistor [tolerance=±5% power=0.25W resistance=1k package=THT]
  LED2 = LED - 3mm [color=bicolore current=0.030A package="3 mm [THT]"]
  U6 = SN74LS32N [package="DIP14 [THT]"]

nets:
  N1: J19.pin1, U8.pin7, U8.pin8, C8.-
  N2: J19.pin2, R17.Pin_1, U8.pin6
  N3: J19.pin3, U8.pin5, C8.+, U7.pin3
  N4: J21.pin1, R8.Pin_0, D1.anode, D2.cathode, J20.pin1
  GND: J21.pin2, U5.GND, LED1.cathode, C4.-, U8.pin3, R9.Pin_0, C2.+, IC2.GND, R4.Pin_1, D5.C, D4.A, R6.Pin_0, R7.Pin_0, D3.anode, C7.-, C3.+, C9.-, C6.+, C1.-, U7.pin2, C11.+, U6.GND
  N5: R14.Pin_0, U5.1Y, C6.-
  N6: R14.Pin_1, U5.2A
  N7: R13.Pin_0, IC1.1B, R18.Pin_0
  VCC: R13.Pin_1, R12.Pin_1, U5.4Y, U5.4A, U5.Vcc, R15.Pin_0, C4.+, IC2.OUT, IC1.1Y, R3.Pin_0, R10.Pin_1, C3.-, C9.+, C10.-, C11.-, U6.1A, U6.2A, U6.3B, U6.4Y, U6.4A, U6.4B, U6.Vcc
  N8: R12.Pin_0, IC1.1A, R19.Pin_0
  N9: U5.1A, R16.Pin_0, U6.1Y
  N10: U5.1B, U5.3B
  N11: U5.2B, R18.Pin_1
  N12: U5.2Y, R19.Pin_1, U6.1B
  N13: U5.3Y, U5.3A, R11.Pin_0, C7.+
  N14: R15.Pin_1, LED1.anode
  N15: R17.Pin_0, J22.pin1, R21.Pin_0
  N16: U8.pin2, R16.Pin_1
  N17: R9.Pin_1, R8.Pin_1, IC1.3Y, IC1.4Y
  N18: R11.Pin_1, IC1.4B, IC1.Vcc, R10.Pin_0
  N19: C2.-, R2.Pin_1, R1.Pin_1
  N20: IC2.IN, D1.cathode, C1.+
  N21: IC1.2A, IC1.GND, D5.A, D4.C, R7.Pin_1, J20.pin2
  N22: IC1.2B, IC1.3B, R5.Pin_1, R6.Pin_1
  N23: IC1.2Y, IC1.3A, R3.Pin_1, R4.Pin_0
  N24: IC1.4A, R2.Pin_0, R5.Pin_0, D3.cathode, C10.+
  N25: R1.Pin_0, D2.anode
  N26: J22.pin2, U7.pin4, R21.Pin_1
  N27: U7.pin1, R20.Pin_1
  N28: R20.Pin_0, R22.Pin_0, U6.2B
  N29: R22.Pin_1, LED2.anode
  N30: LED2.cathode, U6.2Y

notes:
  DCC in
  1
  2
  DCC out
  www.locoduino.org
  © locoduino
  Detection DCC address and direction
  GNDµC
  OUT
  5VµC
  VIO
  DIR
  v3.1 - 10/2026

custom parts:
  Voltage Regulator 78L05 (TO-92, triangle): TO92 78xx voltage regulator. IGO (Input Ground Output). Locoduino DCC-LocoAddr v3.1 : attributs de cuivre portés par chaque pastille (évite le perçage non métallisé parasite à l'export Gerber).
