# Fritzing sketch locoaddr_display_min_v3.0 (saved by Fritzing 1.0.1rc)
circuit board: 5.5cm x 4cm
breadboards: 1

parts:
  U1 = IC, DIP package, 16 pins [chip_label="ESP32-C3 SuperMini"]
  U2 = IC, DIP package, 10 pins [chip_label="Pololu 2595"]
  J3 = male pin header, 4 pins [form="♂ (male)"]
  J4 = Screw terminal - 2 pins [package=THT]
  J5 = Screw terminal - 2 pins [package=THT]
  U4 = Voltage Regulator - 5V [package="TO220 [THT]"]
  J6 = Screw terminal - 2 pins [package=THT]
  D1 = Rectifier Diode [part_number=1N4001 package="300 mil [THT]"]
  C1 = Capacitor Polarized [package=cpol-radial-10uf-25v]

nets:
  N1: U1.pin6, J5.pin2
  N2: U1.pin11, U2.pin8
  N3: U1.pin12, U2.pin7
  N4: U1.pin14, U2.pin6, J4.pin2
  N5: U1.pin15, J3.pin4, J4.pin1, U4.GND, J6.pin1, C1.-
  N6: U1.pin16, U2.pin5, J3.pin3, J5.pin1, D1.cathode
  N7: U2.pin3, J3.pin1
  N8: U2.pin4, J3.pin2
  N9: U4.input_voltage, J6.pin2, C1.+
  N10: U4.output_voltage, D1.anode

notes:
  www.locoduino.org
  © locoduino
  Mini Display DCC address
  USB
  5V
  GND
  3V3
  H
  L
  TM1637
  CLK
  DIO
  VCC
  RX
  VIO
  ALIM IN
  DETECTEUR
  v3.0 - 10/2026
  POLOLU 2595
  ESP32 C3 mini
