# Fritzing sketch locoaddr_detector_v3.11 (saved by Fritzing 1.0.1rc)
circuit board: 10cm x 6.8cm
breadboards: 1

parts:
  J19 = screw terminal, 3 pins
  J21 = Screw terminal - 2 pins [package=THT]
  R14 = Resistor [tolerance=±5% power=0.25W resistance=470 package=THT]
  R13 = Resistor [tolerance=±5% power=0.25W resistance=10k package=THT]
  R12 = Resistor [tolerance=±5% power=0.25W resistance=10k package=THT]
  R15 = Resistor [tolerance=±5% power=0.25W resistance=1k package=THT]
  LED1 = LED - 3mm [color="Green (570nm)" current=0.030A package="3 mm [THT]"]
  C4 = Electrolytic Capacitor [capacitance=100µF voltage=35V package="100 mil [THT, electrolytic]"]
  R17 = Resistor [tolerance=±5% power=0.25W resistance=2.2k package=THT]
  U8 = IC, DIP package, 8 pins [chip_label=6N137]
  R16 = Resistor [tolerance=±5% power=0.25W resistance=270 package=THT]
  R9 = Resistor [tolerance=±5% power=0.25W resistance=1k package=THT]
  R11 = Resistor [tolerance=±5% power=0.25W resistance=470 package=THT]
  R8 = Resistor [tolerance=±5% power=0.25W resistance=100k package=THT]
  C2 = Electrolytic Capacitor [capacitance=100µF voltage=35V package="100 mil [THT, electrolytic]"]
  IC2 = Voltage Regulator 78L05 (TO-92, triangle) [package=to-92]
  R3 = Resistor [tolerance=±5% power=0.25W resistance=270k package=THT]
  R10 = Resistor [tolerance=±5% power=0.25W resistance=10k package=THT]
  R2 = Resistor [tolerance=±5% power=0.25W resistance=1k package=THT]
  R1 = Resistor [tolerance=±5% power=0.25W resistance=1k package=THT]
  R4 = Resistor [tolerance=±5% power=0.25W resistance=1k package=THT]
  D5 = Diode [part_number=SB320 mn=10 package=diode-1n4001]
  D4 = Diode [part_number=SB320 mn=5 package=diode-1n4001]
  R5 = Resistor [tolerance=±5% power=0.25W resistance=33k package=THT]
  R6 = Resistor [tolerance=±5% power=0.25W resistance=820 package=THT]
  R7 = Resistor [tolerance=±5% power=1W resistance=1.8 package=THT]
  D1 = Rectifier Diode [part_number=1N4007 package="300 mil [THT]"]
  D2 = Rectifier Diode [part_number=1N4007 package="300 mil [THT]"]
  D3 = Rectifier Diode [part_number=1N4007 package="300 mil [THT]"]
  C8 = Film/Foil Capacitor [capacitance=100nF voltage=35V package="5mm [THT, pp]"]
  C7 = Film/Foil Capacitor [capacitance=1nF voltage=35V package="5mm [THT, pp]"]
  C3 = Film/Foil Capacitor [capacitance=100nF voltage=35V package="5mm [THT, pp]"]
  C9 = Film/Foil Capacitor [capacitance=100nF voltage=35V package="5mm [THT, pp]"]
  C6 = Film/Foil Capacitor [capacitance=680pF voltage=35V package="5mm [THT, pp]"]
  C1 = Capacitor Polarized [voltage=35V capacitance=220µF package=cpol-radial-100uf-25v]
  J20 = screw terminal, 2 pins
  R18 = Resistor [tolerance=±5% power=0.25W resistance=1k package=THT]
  R19 = Resistor [tolerance=±5% power=0.25W resistance=1k package=THT]
  C10 = Film/Foil Capacitor [capacitance=100nF voltage=35V package="5mm [THT, pp]"]
  J22 = Screw terminal - 2 pins [package=THT]
  U7 = IC, DIP package, 4 pins [chip_label=PC817]
  C11 = Film/Foil Capacitor [capacitance=100nF voltage=35V package="5mm [THT, pp]"]
  R20 = Resistor [tolerance=±5% power=0.25W resistance=1k package=THT]
  R21 = Resistor [tolerance=±5% power=0.25W resistance=4.7k package=THT]
  R22 = Resistor [tolerance=±5% power=0.25W resistance=1k package=THT]
  LED2 = LED - 3mm [color=bicolore current=0.030A package="3 mm [THT]"]
  IC1 = LM339 [chip_label=IC package="DIP (Dual Inline) [THT]"]
  IC1_PWR = LM339 [package="DIP (Dual Inline) [THT]"]  # not connected
  IC1_A = LM339 [package="DIP (Dual Inline) [THT]"]  # not connected
  IC1_B = LM339 [package="DIP (Dual Inline) [THT]"]  # not connected
  IC1_C = LM339 [package="DIP (Dual Inline) [THT]"]  # not connected
  IC1_D = LM339 [package="DIP (Dual Inline) [THT]"]  # not connected
  U5 = 74HC02 [part_number=SN74HC02N package="DIP14 [THT]"]
  U6 = 74LS74-Flipflops [part_number=74HC74 package="DIP (Dual Inline) [THT]"]
  part = 74LS74-Flipflops [part_number=74LS74 package="DIP (Dual Inline) [THT]"]  # not connected
  U6_1 = 74LS74-Flipflops [part_number=74LS74 package="DIP (Dual Inline) [THT]"]  # not connected
  U6_2 = 74LS74-Flipflops [part_number=74LS74 package="DIP (Dual Inline) [THT]"]  # not connected

nets:
  N1: J19.pin1, U8.pin7, U8.pin8, C8.-
  N2: J19.pin2, R17.Pin_1, U8.pin6
  N3: J19.pin3, U8.pin5, C8.+, U7.pin3
  N4: J21.pin1, R8.Pin_0, D1.anode, D2.cathode, J20.pin1
  GND: J21.pin2, LED1.cathode, C4.-, U8.pin3, R9.Pin_0, C2.+, IC2.GND, R4.Pin_1, D5.C, D4.A, R6.Pin_0, R7.Pin_0, D3.anode, C7.-, C3.+, C9.-, C6.+, C1.-, U7.pin2, C11.+, U5.GND, U6.connector6
  N5: R14.Pin_0, C6.-, U5.1B
  N6: R14.Pin_1, U5.2Y
  N7: R13.Pin_0, R18.Pin_0, IC1.connector1
  N8: R13.Pin_1, R12.Pin_1, R15.Pin_0, C4.+, IC2.OUT, R3.Pin_0, R10.Pin_1, C3.-, C9.+, C10.-, C11.-, IC1.connector2, U5.4A, U5.4B, U5.VCC, U6.connector0, U6.connector3, U6.connector9, U6.connector10, U6.connector11, U6.connector12, U6.connector13
  N9: R12.Pin_0, R19.Pin_0, IC1.connector0
  N10: R15.Pin_1, LED1.anode
  N11: R17.Pin_0, J22.pin1, R21.Pin_0
  N12: U8.pin2, R16.Pin_1
  N13: R16.Pin_0, U5.1Y, U6.connector2
  N14: R9.Pin_1, R8.Pin_1, IC1.connector7, IC1.connector10
  N15: R11.Pin_0, C7.+, U5.3A, U5.3B
  N16: R11.Pin_1, R10.Pin_0, IC1.connector12, IC1.connector13
  N17: C2.-, R2.Pin_1, R1.Pin_1
  N18: IC2.IN, D1.cathode, C1.+
  N19: R3.Pin_1, R4.Pin_0, IC1.connector5, IC1.connector8
  N20: R2.Pin_0, R5.Pin_0, D3.cathode, C10.+, IC1.connector11
  N21: R1.Pin_0, D2.anode
  N22: D5.A, D4.C, R7.Pin_1, J20.pin2, IC1.connector3, IC1.connector6
  N23: R5.Pin_1, R6.Pin_1, IC1.connector4, IC1.connector9
  N24: R18.Pin_1, U5.2A
  N25: R19.Pin_1, U5.2B, U6.connector1
  N26: J22.pin2, U7.pin4, R21.Pin_1
  N27: U7.pin1, R20.Pin_1
  N28: R20.Pin_0, R22.Pin_0, U6.connector4
  N29: R22.Pin_1, LED2.anode
  N30: LED2.cathode, U6.connector5
  N31: U5.1A, U5.3Y

notes:
  DCC in
  1
  2
  DCC out
  www.locoduino.org
  © locoduino
  Detection DCC address and direction
  GNDµC
  OUT
  5VµC
  VIO
  DIR
  v3.11 - 11/2026

custom parts:
  Voltage Regulator 78L05 (TO-92, triangle): TO92 78xx voltage regulator. IGO (Input Ground Output). Locoduino DCC-LocoAddr v3.1 : attributs de cuivre portés par chaque pastille (évite le perçage non métallisé parasite à l'export Gerber).
  LM339: A Quad Norton Op AMp
  LM339: A Quad Norton Op AMp
  LM339: A Quad Norton Op AMp
  LM339: A Quad Norton Op AMp
  LM339: A Quad Norton Op AMp
  LM339: A Quad Norton Op AMp
  74HC02: Quad 2 input NOR logic gates
