# Fritzing sketch locoaddr_display_v2.1 (saved by Fritzing 1.0.1rc)
circuit board: 10cm x 7cm
breadboards: 1

parts:
  J11 = female pin header, 19 pins [form="♀ (female)"]
  J21 = female pin header, 19 pins [form="♀ (female)"]
  1KΩ = Resistor [tolerance=±5% resistance=220 power=0.25W package=THT]
  1KΩ_2 = Resistor [tolerance=±5% resistance=220 power=0.25W package=THT]
  1KΩ_3 = Resistor [tolerance=±5% resistance=220 power=0.25W package=THT]
  2N2222 = NPN-Transistor [package="TO92 [THT]"]
  J24 = screw terminal, 3 pins
  Pad58 = Pad [width=3 height=3 connect=center]
  Pad59 = Pad [width=3 height=3 connect=center]
  Pad60 = Pad [width=3 height=3 connect=center]
  Pad61 = Pad [width=3 height=3 connect=center]
  Pad62 = Pad [width=3 height=3 connect=center]
  J23 = female pin header, 6 pins [form="♀ (female)"]
  J22 = female pin header, 6 pins [form="♀ (female)"]
  2N2222_2 = NPN-Transistor [package="TO92 [THT]"]
  1KΩ_4 = Resistor [tolerance=±5% resistance=220 power=0.25W package=THT]
  2N2222_3 = NPN-Transistor [package="TO92 [THT]"]
  2N2222_4 = NPN-Transistor [package="TO92 [THT]"]
  68Ω = Resistor [tolerance=±5% resistance=220 power=0.25W package=THT]
  68Ω_2 = Resistor [tolerance=±5% resistance=220 power=0.25W package=THT]
  68Ω_3 = Resistor [tolerance=±5% resistance=220 power=0.25W package=THT]
  68Ω_4 = Resistor [tolerance=±5% resistance=220 power=0.25W package=THT]
  68Ω_5 = Resistor [tolerance=±5% resistance=220 power=0.25W package=THT]
  68Ω_6 = Resistor [tolerance=±5% resistance=220 power=0.25W package=THT]
  68Ω_7 = Resistor [tolerance=±5% resistance=220 power=0.25W package=THT]

nets:
  N1: J11.pin1, Pad58.pad
  N2: J11.pin9, 1KΩ_3.Pin_1
  N3: J11.pin10, 1KΩ_4.Pin_0
  N4: J11.pin11, 68Ω_7.Pin_0
  N5: J11.pin12, 1KΩ_2.Pin_0
  N6: J11.pin13, 1KΩ.Pin_0
  N7: J11.pin14, 2N2222.C, J24.pin3, Pad62.pad, 2N2222_2.C, 2N2222_3.C, 2N2222_4.C
  N8: J11.pin15, 68Ω_6.Pin_0
  N9: J11.pin19, J24.pin1, Pad60.pad, Pad61.pad
  N10: J21.pin1, Pad59.pad
  N11: J21.pin2, 68Ω_5.Pin_1
  N12: J21.pin3, 68Ω_4.Pin_1
  N13: J21.pin6, 68Ω_3.Pin_1
  N14: J21.pin8, 68Ω_2.Pin_1
  N15: J21.pin9, 68Ω.Pin_1
  N16: J21.pin13, J24.pin2
  N17: 1KΩ.Pin_1, 2N2222.B
  N18: 1KΩ_2.Pin_1, 2N2222_2.B
  N19: 1KΩ_3.Pin_0, 2N2222_4.B
  N20: 2N2222.E, J22.pin3
  N21: J23.pin1, 2N2222_3.E
  N22: J23.pin2, 68Ω.Pin_0
  N23: J23.pin3, 68Ω_2.Pin_0
  N24: J23.pin5, 68Ω_3.Pin_0
  N25: J23.pin6, 68Ω_4.Pin_0
  N26: J22.pin1, 68Ω_5.Pin_0
  N27: J22.pin2, 2N2222_4.E
  N28: J22.pin4, 68Ω_7.Pin_1
  N29: J22.pin5, 68Ω_6.Pin_1
  N30: J22.pin6, 2N2222_2.E
  N31: 1KΩ_4.Pin_1, 2N2222_3.B

notes:
  12
  14
  27
  13
  GND
  VIN-5V
  26
  25
  33
  32
  23
  22
  21
  19
  18
  3.3V
  www.locoduino.org
  © locoduino v 2.1 - 06/2025
  Display DCC address
  GND  RX  +5V
  +5V +5V
  1
  6
  4
  5
  WENRUN LFD039AUE-102A-01
